# Fritzing sketch sensorstation-wiring (saved by Fritzing 0.9.3b)
breadboards: 1

parts:
  Raspberry_Pi_1 = Raspberry Pi 3 [part_number=RPI-3-V1.2]
  MQ-135 = GAS_SENSOR [package=mq-3]
  Part1 = Adafruit ADS1115 16Bit I2C ADC [part_number="Adafruit #1085"]
  Part2 = Adafruit TSL2561 [part_number="Adafruit #439"]
  Part3 = Barometric Pressure Sensor - BMP180 Breakout (GY-68)
  Part4 = Adafruit SHT31-D Sensirion Temperature/Humidity Sensor [part_number="Adafruit #2857"]

nets:
  3V3: Raspberry_Pi_1.3v3, Raspberry_Pi_1.3V3, Part1.VDD, Part2.3.3V, Part4.VIN
  N1: Raspberry_Pi_1.GPIO2, Part1.SDA, Part2.SDA, Part3.SDA, Part4.SDA
  GND: Raspberry_Pi_1.GPIO3, Raspberry_Pi_1.GND, MQ-135.A1, Part1.SCL, Part1.GND, Part2.GND, Part2.SCL, Part3.GND, Part3.SCL, Part4.GND, Part4.SCL
  5V: Raspberry_Pi_1.5V, MQ-135.B1, Part3.VCC

notes:
  3.3V
  5V
  ADC
  Light
  Pressure
  Temperature
  Humidity
  Air quality

custom parts:
  Adafruit ADS1115 16Bit I2C ADC: For microcontrollers without an analog-to-digital converter or when you want a higher-precision ADC, the ADS1115 provides 16-bit precision at 860 samples/second over I2C. The chip can be configured as 4 single-ended input channels, or two differential channels. As a nice bonus, it even includes a programmable gain amplifier, up to x16, to help boost up smaller single/differential signals to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
  Adafruit TSL2561: The TSL2561 luminosity sensor is an advanced digital light sensor, ideal for use in a wide range of light situations. Compared to low cost CdS cells, this sensor is more precise, allowing for exact lux calculations and can be configured for different gain/timing ranges to detect light ranges from up to 0.1 - 40,000+ Lux on the fly. The best part of this sensor is that it contains both infrared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
  Adafruit SHT31-D Sensirion Temperature/Humidity Sensor: Sensirion Temperature/Humidity sensors are some of the finest & highest-accuracy devices you can get. And, finally we have some that have a true I2C interface for easy reading. The SHT31-D sensor has an excellent ±2% relative humidity and ±0.3°C accuracy for most uses. Unlike earlier SHT sensors, this sensor has a true I2C interface, and (bonus!) even with two address options. It also is 3V or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
